// Logisim project FirstGatesProject.circ as structural Verilog: 16 circuits, main circuit notCircuit
module notCircuit (
  input  in_1,
  output out_2
);

  nand nand_1 (out_2, in_1, in_1);
endmodule

module andGate (
  input  in_1,
  input  in_2,
  output out_3
);

  wire nand_1_out;

  nand nand_1 (nand_1_out, in_1, in_2);
  notCircuit notcircuit_1 (.in_1(nand_1_out), .out_2(out_3));
endmodule

module orCircuit (
  input  in_1,
  input  in_2,
  output out_3
);

  wire notcircuit_1_out_2, notcircuit_2_out_2;

  notCircuit notcircuit_1 (.in_1(in_1), .out_2(notcircuit_1_out_2));
  notCircuit notcircuit_2 (.in_1(in_2), .out_2(notcircuit_2_out_2));
  nand nand_1 (out_3, notcircuit_1_out_2, notcircuit_2_out_2);
endmodule

module xorCircuit (
  input  in_1,
  input  in_2,
  output out_3
);

  wire nand_1_out, orcircuit_1_out_3;

  orCircuit orcircuit_1 (.in_1(in_1), .in_2(in_2), .out_3(orcircuit_1_out_3));
  nand nand_1 (nand_1_out, in_1, in_2);
  andGate andgate_1 (.in_1(orcircuit_1_out_3), .in_2(nand_1_out), .out_3(out_3));
endmodule

module Mux (
  input  a,
  input  b,
  input  sel,
  output out_4
);

  wire andgate_1_out_3, andgate_2_out_3, notcircuit_1_out_2;

  notCircuit notcircuit_1 (.in_1(sel), .out_2(notcircuit_1_out_2));
  andGate andgate_1 (.in_1(b), .in_2(sel), .out_3(andgate_1_out_3));
  andGate andgate_2 (.in_1(a), .in_2(notcircuit_1_out_2), .out_3(andgate_2_out_3));
  orCircuit orcircuit_1 (.in_1(andgate_2_out_3), .in_2(andgate_1_out_3), .out_3(out_4));
endmodule

module dmux (
  input  i_n,
  input  sel,
  output a,
  output b
);

  wire notcircuit_1_out_2;

  notCircuit notcircuit_1 (.in_1(sel), .out_2(notcircuit_1_out_2));
  andGate andgate_1 (.in_1(i_n), .in_2(notcircuit_1_out_2), .out_3(a));
  andGate andgate_2 (.in_1(i_n), .in_2(sel), .out_3(b));
endmodule

module not16 (
  input  [15:0] in_1,
  output [15:0] out_2
);

  notCircuit notcircuit_1 (.in_1(in_1[0]), .out_2(out_2[0]));
  notCircuit notcircuit_2 (.in_1(in_1[1]), .out_2(out_2[1]));
  notCircuit notcircuit_3 (.in_1(in_1[2]), .out_2(out_2[2]));
  notCircuit notcircuit_4 (.in_1(in_1[3]), .out_2(out_2[3]));
  notCircuit notcircuit_5 (.in_1(in_1[4]), .out_2(out_2[4]));
  notCircuit notcircuit_6 (.in_1(in_1[5]), .out_2(out_2[5]));
  notCircuit notcircuit_7 (.in_1(in_1[6]), .out_2(out_2[6]));
  notCircuit notcircuit_8 (.in_1(in_1[7]), .out_2(out_2[7]));
  notCircuit notcircuit_9 (.in_1(in_1[8]), .out_2(out_2[8]));
  notCircuit notcircuit_10 (.in_1(in_1[9]), .out_2(out_2[9]));
  notCircuit notcircuit_11 (.in_1(in_1[10]), .out_2(out_2[10]));
  notCircuit notcircuit_12 (.in_1(in_1[11]), .out_2(out_2[11]));
  notCircuit notcircuit_13 (.in_1(in_1[12]), .out_2(out_2[12]));
  notCircuit notcircuit_14 (.in_1(in_1[13]), .out_2(out_2[13]));
  notCircuit notcircuit_15 (.in_1(in_1[14]), .out_2(out_2[14]));
  notCircuit notcircuit_16 (.in_1(in_1[15]), .out_2(out_2[15]));
endmodule

module and16 (
  input  [15:0] in_1,
  input  [15:0] in_2,
  output [15:0] out_3
);

  andGate andgate_1 (.in_1(in_2[0]), .in_2(in_1[0]), .out_3(out_3[0]));
  andGate andgate_2 (.in_1(in_2[1]), .in_2(in_1[1]), .out_3(out_3[1]));
  andGate andgate_3 (.in_1(in_2[2]), .in_2(in_1[2]), .out_3(out_3[2]));
  andGate andgate_4 (.in_1(in_2[3]), .in_2(in_1[3]), .out_3(out_3[3]));
  andGate andgate_5 (.in_1(in_2[4]), .in_2(in_1[4]), .out_3(out_3[4]));
  andGate andgate_6 (.in_1(in_2[5]), .in_2(in_1[5]), .out_3(out_3[5]));
  andGate andgate_7 (.in_1(in_2[6]), .in_2(in_1[6]), .out_3(out_3[6]));
  andGate andgate_8 (.in_1(in_2[7]), .in_2(in_1[7]), .out_3(out_3[7]));
  andGate andgate_9 (.in_1(in_2[8]), .in_2(in_1[8]), .out_3(out_3[8]));
  andGate andgate_10 (.in_1(in_2[9]), .in_2(in_1[9]), .out_3(out_3[9]));
  andGate andgate_11 (.in_1(in_2[10]), .in_2(in_1[10]), .out_3(out_3[10]));
  andGate andgate_12 (.in_1(in_2[11]), .in_2(in_1[11]), .out_3(out_3[11]));
  andGate andgate_13 (.in_1(in_2[12]), .in_2(in_1[12]), .out_3(out_3[12]));
  andGate andgate_14 (.in_1(in_2[13]), .in_2(in_1[13]), .out_3(out_3[13]));
  andGate andgate_15 (.in_1(in_2[14]), .in_2(in_1[14]), .out_3(out_3[14]));
  andGate andgate_16 (.in_1(in_2[15]), .in_2(in_1[15]), .out_3(out_3[15]));
endmodule

module or16 (
  input  [15:0] in_1,
  input  [15:0] in_2,
  output [15:0] out_3
);

  orCircuit orcircuit_1 (.in_1(in_2[0]), .in_2(in_1[0]), .out_3(out_3[0]));
  orCircuit orcircuit_2 (.in_1(in_2[1]), .in_2(in_1[1]), .out_3(out_3[1]));
  orCircuit orcircuit_3 (.in_1(in_2[2]), .in_2(in_1[2]), .out_3(out_3[2]));
  orCircuit orcircuit_4 (.in_1(in_2[3]), .in_2(in_1[3]), .out_3(out_3[3]));
  orCircuit orcircuit_5 (.in_1(in_2[4]), .in_2(in_1[4]), .out_3(out_3[4]));
  orCircuit orcircuit_6 (.in_1(in_2[5]), .in_2(in_1[5]), .out_3(out_3[5]));
  orCircuit orcircuit_7 (.in_1(in_2[6]), .in_2(in_1[6]), .out_3(out_3[6]));
  orCircuit orcircuit_8 (.in_1(in_2[7]), .in_2(in_1[7]), .out_3(out_3[7]));
  orCircuit orcircuit_9 (.in_1(in_2[8]), .in_2(in_1[8]), .out_3(out_3[8]));
  orCircuit orcircuit_10 (.in_1(in_2[9]), .in_2(in_1[9]), .out_3(out_3[9]));
  orCircuit orcircuit_11 (.in_1(in_2[10]), .in_2(in_1[10]), .out_3(out_3[10]));
  orCircuit orcircuit_12 (.in_1(in_2[11]), .in_2(in_1[11]), .out_3(out_3[11]));
  orCircuit orcircuit_13 (.in_1(in_2[12]), .in_2(in_1[12]), .out_3(out_3[12]));
  orCircuit orcircuit_14 (.in_1(in_2[13]), .in_2(in_1[13]), .out_3(out_3[13]));
  orCircuit orcircuit_15 (.in_1(in_2[14]), .in_2(in_1[14]), .out_3(out_3[14]));
  orCircuit orcircuit_16 (.in_1(in_2[15]), .in_2(in_1[15]), .out_3(out_3[15]));
endmodule

module or8way (
  input  [7:0] in_1,
  output out_2
);

  wire orcircuit_1_out_3, orcircuit_2_out_3, orcircuit_3_out_3, orcircuit_4_out_3, orcircuit_5_out_3,
       orcircuit_6_out_3;

  orCircuit orcircuit_1 (.in_1(in_1[0]), .in_2(in_1[1]), .out_3(orcircuit_1_out_3));
  orCircuit orcircuit_2 (.in_1(orcircuit_1_out_3), .in_2(orcircuit_3_out_3), .out_3(orcircuit_2_out_3));
  orCircuit orcircuit_3 (.in_1(in_1[2]), .in_2(in_1[3]), .out_3(orcircuit_3_out_3));
  orCircuit orcircuit_4 (.in_1(in_1[4]), .in_2(in_1[5]), .out_3(orcircuit_4_out_3));
  orCircuit orcircuit_5 (.in_1(orcircuit_4_out_3), .in_2(orcircuit_6_out_3), .out_3(orcircuit_5_out_3));
  orCircuit orcircuit_6 (.in_1(in_1[6]), .in_2(in_1[7]), .out_3(orcircuit_6_out_3));
  orCircuit orcircuit_7 (.in_1(orcircuit_2_out_3), .in_2(orcircuit_5_out_3), .out_3(out_2));
endmodule

module mux16 (
  input  [15:0] a,
  input  [15:0] b,
  input  sel,
  output [15:0] out_4
);

  wire [15:0] and16_1_out_3, and16_2_out_3, not16_1_out_2, to16_1_out_2;

  to16 to16_1 (.in_1(sel), .out_2(to16_1_out_2));
  and16 and16_1 (.in_1(a), .in_2(not16_1_out_2), .out_3(and16_1_out_3));
  not16 not16_1 (.in_1(to16_1_out_2), .out_2(not16_1_out_2));
  and16 and16_2 (.in_1(b), .in_2(to16_1_out_2), .out_3(and16_2_out_3));
  or16 or16_1 (.in_1(and16_1_out_3), .in_2(and16_2_out_3), .out_3(out_4));
endmodule

module mux4way16 (
  input  [15:0] a,
  input  [15:0] b,
  input  [1:0] sel,
  input  [15:0] c,
  input  [15:0] d,
  output [15:0] out_6
);

  wire [15:0] mux16_1_out_4, mux16_2_out_4;

  mux16 mux16_1 (.a(a), .b(b), .sel(sel[0]), .out_4(mux16_1_out_4));
  mux16 mux16_2 (.a(c), .b(d), .sel(sel[0]), .out_4(mux16_2_out_4));
  mux16 mux16_3 (.a(mux16_1_out_4), .b(mux16_2_out_4), .sel(sel[1]), .out_4(out_6));
endmodule

module to16 (
  input  in_1,
  output [15:0] out_2
);


  assign out_2 = {16{in_1}};
endmodule

module mux8way16 (
  input  [15:0] a,
  input  [15:0] b,
  input  [15:0] c,
  input  [15:0] d,
  input  [2:0] sel,
  input  [15:0] e,
  input  [15:0] f,
  input  [15:0] g,
  input  [15:0] h,
  output [15:0] out_10
);

  wire [15:0] mux4way16_1_out_6, mux4way16_2_out_6;

  mux4way16 mux4way16_1 (.a(a), .b(b), .sel(sel[1:0]), .c(c), .d(d), .out_6(mux4way16_1_out_6));
  mux4way16 mux4way16_2 (.a(e), .b(f), .sel(sel[1:0]), .c(g), .d(h), .out_6(mux4way16_2_out_6));
  mux16 mux16_1 (.a(mux4way16_1_out_6), .b(mux4way16_2_out_6), .sel(sel[2]), .out_4(out_10));
endmodule

module dmux4way (
  input  i_n,
  input  [1:0] sel,
  output a,
  output b,
  output c,
  output d
);

  wire dmux_1_a, dmux_1_b;

  dmux dmux_1 (.i_n(i_n), .sel(sel[1]), .a(dmux_1_a), .b(dmux_1_b));
  dmux dmux_2 (.i_n(dmux_1_a), .sel(sel[0]), .a(a), .b(b));
  dmux dmux_3 (.i_n(dmux_1_b), .sel(sel[0]), .a(c), .b(d));
endmodule

module dmux8way (
  input  i_n,
  input  [2:0] sel,
  output a,
  output b,
  output c,
  output d,
  output e,
  output f,
  output g,
  output h
);

  wire dmux_1_a, dmux_1_b;

  dmux dmux_1 (.i_n(i_n), .sel(sel[2]), .a(dmux_1_a), .b(dmux_1_b));
  dmux4way dmux4way_1 (.i_n(dmux_1_a), .sel(sel[1:0]), .a(a), .b(b), .c(c), .d(d));
  dmux4way dmux4way_2 (.i_n(dmux_1_b), .sel(sel[1:0]), .a(e), .b(f), .c(g), .d(h));
endmodule
