// Logisim project MemoryProject.circ as structural Verilog: 3 circuits, main circuit bit
module \bit  (
  input  i_n,
  input  clock,
  input  load,
  output ou_t
);

  wire multiplexer_1_out;

  D_Flip_Flop d_ff_1 (.D(multiplexer_1_out), .clk(clock), .Q(ou_t));  // open: Qn, preset, reset
  Multiplexer multiplexer_1 (.in0(i_n), .in1(ou_t), .out(multiplexer_1_out), .sel(load));
endmodule

module register16 (
  input  load,
  input  clock,
  input  [15:0] in_3,
  output [15:0] out_4
);

  \bit  bit_1 (.i_n(in_3[0]), .load(load), .clock(clock), .ou_t(out_4[0]));
  \bit  bit_2 (.i_n(in_3[1]), .load(load), .clock(clock), .ou_t(out_4[1]));
  \bit  bit_3 (.i_n(in_3[2]), .load(load), .clock(clock), .ou_t(out_4[2]));
  \bit  bit_4 (.i_n(in_3[3]), .load(load), .clock(clock), .ou_t(out_4[3]));
  \bit  bit_5 (.i_n(in_3[4]), .load(load), .clock(clock), .ou_t(out_4[4]));
  \bit  bit_6 (.i_n(in_3[5]), .load(load), .clock(clock), .ou_t(out_4[5]));
  \bit  bit_7 (.i_n(in_3[6]), .load(load), .clock(clock), .ou_t(out_4[6]));
  \bit  bit_8 (.i_n(in_3[7]), .load(load), .clock(clock), .ou_t(out_4[7]));
  \bit  bit_9 (.i_n(in_3[8]), .load(load), .clock(clock), .ou_t(out_4[8]));
  \bit  bit_10 (.i_n(in_3[9]), .load(load), .clock(clock), .ou_t(out_4[9]));
  \bit  bit_11 (.i_n(in_3[10]), .load(load), .clock(clock), .ou_t(out_4[10]));
  \bit  bit_12 (.i_n(in_3[11]), .load(load), .clock(clock), .ou_t(out_4[11]));
  \bit  bit_13 (.i_n(in_3[12]), .load(load), .clock(clock), .ou_t(out_4[12]));
  \bit  bit_14 (.i_n(in_3[13]), .load(load), .clock(clock), .ou_t(out_4[13]));
  \bit  bit_15 (.i_n(in_3[14]), .load(load), .clock(clock), .ou_t(out_4[14]));
  \bit  bit_16 (.i_n(in_3[15]), .load(load), .clock(clock), .ou_t(out_4[15]));
endmodule

module Ram8 (
  input  load,
  input  [15:0] i_n,
  input  [2:0] address,
  input  clock,
  output [15:0] out_5
);

  wire demultiplexer_1_out0, demultiplexer_1_out1, demultiplexer_1_out2, demultiplexer_1_out3,
       demultiplexer_1_out4, demultiplexer_1_out5, demultiplexer_1_out6, demultiplexer_1_out7;
  wire [15:0] demultiplexer_2_out0, demultiplexer_2_out1, demultiplexer_2_out2, demultiplexer_2_out3,
       demultiplexer_2_out4, demultiplexer_2_out5, demultiplexer_2_out6, demultiplexer_2_out7,
       register16_1_out_4, register16_2_out_4, register16_3_out_4, register16_4_out_4, register16_5_out_4,
       register16_6_out_4, register16_7_out_4, register16_8_out_4;

  Demultiplexer #(.select(3)) demultiplexer_1 (
    .out0(demultiplexer_1_out0), .out1(demultiplexer_1_out1), .out2(demultiplexer_1_out2),
    .out3(demultiplexer_1_out3), .out4(demultiplexer_1_out4), .out5(demultiplexer_1_out5),
    .out6(demultiplexer_1_out6), .out7(demultiplexer_1_out7), .in(load), .sel(address));
  Demultiplexer #(.select(3), .width(16)) demultiplexer_2 (
    .out0(demultiplexer_2_out0), .out1(demultiplexer_2_out1), .out2(demultiplexer_2_out2),
    .out3(demultiplexer_2_out3), .out4(demultiplexer_2_out4), .out5(demultiplexer_2_out5),
    .out6(demultiplexer_2_out6), .out7(demultiplexer_2_out7), .in(i_n), .sel(address));
  register16 register16_1 (
    .load(demultiplexer_1_out0), .clock(clock), .in_3(demultiplexer_2_out0), .out_4(register16_1_out_4));
  register16 register16_2 (
    .load(demultiplexer_1_out1), .clock(clock), .in_3(demultiplexer_2_out1), .out_4(register16_2_out_4));
  register16 register16_3 (
    .load(demultiplexer_1_out2), .clock(clock), .in_3(demultiplexer_2_out2), .out_4(register16_3_out_4));
  register16 register16_4 (
    .load(demultiplexer_1_out3), .clock(clock), .in_3(demultiplexer_2_out3), .out_4(register16_4_out_4));
  register16 register16_5 (
    .load(demultiplexer_1_out4), .clock(clock), .in_3(demultiplexer_2_out4), .out_4(register16_5_out_4));
  register16 register16_6 (
    .load(demultiplexer_1_out5), .clock(clock), .in_3(demultiplexer_2_out5), .out_4(register16_6_out_4));
  register16 register16_7 (
    .load(demultiplexer_1_out6), .clock(clock), .in_3(demultiplexer_2_out6), .out_4(register16_7_out_4));
  register16 register16_8 (
    .load(demultiplexer_1_out7), .clock(clock), .in_3(demultiplexer_2_out7), .out_4(register16_8_out_4));
  Multiplexer #(.select(3), .width(16)) multiplexer_1 (
    .in0(register16_1_out_4), .in1(register16_2_out_4), .in2(register16_3_out_4), .in3(register16_4_out_4),
    .in4(register16_5_out_4), .in5(register16_6_out_4), .in6(register16_7_out_4), .in7(register16_8_out_4),
    .out(out_5), .sel(address));
endmodule
