// Logisim project MemoryProject.circ as structural Verilog: 7 circuits, main circuit bit
module \bit  (
  input  i_n,
  input  clock,
  input  load,
  output ou_t
);

  wire multiplexer_1_out;

  D_Flip_Flop d_ff_1 (.D(multiplexer_1_out), .clk(clock), .Q(ou_t));  // open: Qn, preset, reset
  Multiplexer multiplexer_1 (.in0(i_n), .in1(ou_t), .out(multiplexer_1_out), .sel(load));
endmodule

module register16 (
  input  load,
  input  clock,
  input  [15:0] in_3,
  output [15:0] ou_t
);

  \bit  bit_1 (.i_n(in_3[0]), .load(load), .clock(clock), .ou_t(ou_t[0]));
  \bit  bit_2 (.i_n(in_3[1]), .load(load), .clock(clock), .ou_t(ou_t[1]));
  \bit  bit_3 (.i_n(in_3[2]), .load(load), .clock(clock), .ou_t(ou_t[2]));
  \bit  bit_4 (.i_n(in_3[3]), .load(load), .clock(clock), .ou_t(ou_t[3]));
  \bit  bit_5 (.i_n(in_3[4]), .load(load), .clock(clock), .ou_t(ou_t[4]));
  \bit  bit_6 (.i_n(in_3[5]), .load(load), .clock(clock), .ou_t(ou_t[5]));
  \bit  bit_7 (.i_n(in_3[6]), .load(load), .clock(clock), .ou_t(ou_t[6]));
  \bit  bit_8 (.i_n(in_3[7]), .load(load), .clock(clock), .ou_t(ou_t[7]));
  \bit  bit_9 (.i_n(in_3[8]), .load(load), .clock(clock), .ou_t(ou_t[8]));
  \bit  bit_10 (.i_n(in_3[9]), .load(load), .clock(clock), .ou_t(ou_t[9]));
  \bit  bit_11 (.i_n(in_3[10]), .load(load), .clock(clock), .ou_t(ou_t[10]));
  \bit  bit_12 (.i_n(in_3[11]), .load(load), .clock(clock), .ou_t(ou_t[11]));
  \bit  bit_13 (.i_n(in_3[12]), .load(load), .clock(clock), .ou_t(ou_t[12]));
  \bit  bit_14 (.i_n(in_3[13]), .load(load), .clock(clock), .ou_t(ou_t[13]));
  \bit  bit_15 (.i_n(in_3[14]), .load(load), .clock(clock), .ou_t(ou_t[14]));
  \bit  bit_16 (.i_n(in_3[15]), .load(load), .clock(clock), .ou_t(ou_t[15]));
endmodule

module Ram8 (
  input  load,
  input  [15:0] i_n,
  input  [2:0] address,
  input  clock,
  output [15:0] out_5
);

  wire demultiplexer_1_out0, demultiplexer_1_out1, demultiplexer_1_out2, demultiplexer_1_out3,
       demultiplexer_1_out4, demultiplexer_1_out5, demultiplexer_1_out6, demultiplexer_1_out7;
  wire [15:0] demultiplexer_2_out0, demultiplexer_2_out1, demultiplexer_2_out2, demultiplexer_2_out3,
       demultiplexer_2_out4, demultiplexer_2_out5, demultiplexer_2_out6, demultiplexer_2_out7,
       register16_1_ou_t, register16_2_ou_t, register16_3_ou_t, register16_4_ou_t, register16_5_ou_t,
       register16_6_ou_t, register16_7_ou_t, register16_8_ou_t;

  Demultiplexer #(.select(3)) demultiplexer_1 (
    .out0(demultiplexer_1_out0), .out1(demultiplexer_1_out1), .out2(demultiplexer_1_out2),
    .out3(demultiplexer_1_out3), .out4(demultiplexer_1_out4), .out5(demultiplexer_1_out5),
    .out6(demultiplexer_1_out6), .out7(demultiplexer_1_out7), .in(load), .sel(address));
  Demultiplexer #(.select(3), .width(16)) demultiplexer_2 (
    .out0(demultiplexer_2_out0), .out1(demultiplexer_2_out1), .out2(demultiplexer_2_out2),
    .out3(demultiplexer_2_out3), .out4(demultiplexer_2_out4), .out5(demultiplexer_2_out5),
    .out6(demultiplexer_2_out6), .out7(demultiplexer_2_out7), .in(i_n), .sel(address));
  register16 register16_1 (
    .load(demultiplexer_1_out0), .clock(clock), .in_3(demultiplexer_2_out0), .ou_t(register16_1_ou_t));
  register16 register16_2 (
    .load(demultiplexer_1_out1), .clock(clock), .in_3(demultiplexer_2_out1), .ou_t(register16_2_ou_t));
  register16 register16_3 (
    .load(demultiplexer_1_out2), .clock(clock), .in_3(demultiplexer_2_out2), .ou_t(register16_3_ou_t));
  register16 register16_4 (
    .load(demultiplexer_1_out3), .clock(clock), .in_3(demultiplexer_2_out3), .ou_t(register16_4_ou_t));
  register16 register16_5 (
    .load(demultiplexer_1_out4), .clock(clock), .in_3(demultiplexer_2_out4), .ou_t(register16_5_ou_t));
  register16 register16_6 (
    .load(demultiplexer_1_out5), .clock(clock), .in_3(demultiplexer_2_out5), .ou_t(register16_6_ou_t));
  register16 register16_7 (
    .load(demultiplexer_1_out6), .clock(clock), .in_3(demultiplexer_2_out6), .ou_t(register16_7_ou_t));
  register16 register16_8 (
    .load(demultiplexer_1_out7), .clock(clock), .in_3(demultiplexer_2_out7), .ou_t(register16_8_ou_t));
  Multiplexer #(.select(3), .width(16)) multiplexer_1 (
    .in0(register16_1_ou_t), .in1(register16_2_ou_t), .in2(register16_3_ou_t), .in3(register16_4_ou_t),
    .in4(register16_5_ou_t), .in5(register16_6_ou_t), .in6(register16_7_ou_t), .in7(register16_8_ou_t),
    .out(out_5), .sel(address));
endmodule

module Ram64 (
  input  load,
  input  [15:0] i_n,
  input  [5:0] address,
  input  clock,
  output [15:0] out_5
);

  wire demultiplexer_1_out0, demultiplexer_1_out1, demultiplexer_1_out2, demultiplexer_1_out3,
       demultiplexer_1_out4, demultiplexer_1_out5, demultiplexer_1_out6, demultiplexer_1_out7;
  wire [15:0] demultiplexer_2_out0, demultiplexer_2_out1, demultiplexer_2_out2, demultiplexer_2_out3,
       demultiplexer_2_out4, demultiplexer_2_out5, demultiplexer_2_out6, demultiplexer_2_out7, ram8_1_out_5,
       ram8_2_out_5, ram8_3_out_5, ram8_4_out_5, ram8_5_out_5, ram8_6_out_5, ram8_7_out_5, ram8_8_out_5;

  Demultiplexer #(.select(3)) demultiplexer_1 (
    .out0(demultiplexer_1_out0), .out1(demultiplexer_1_out1), .out2(demultiplexer_1_out2),
    .out3(demultiplexer_1_out3), .out4(demultiplexer_1_out4), .out5(demultiplexer_1_out5),
    .out6(demultiplexer_1_out6), .out7(demultiplexer_1_out7), .in(load), .sel(address[5:3]));
  Demultiplexer #(.select(3), .width(16)) demultiplexer_2 (
    .out0(demultiplexer_2_out0), .out1(demultiplexer_2_out1), .out2(demultiplexer_2_out2),
    .out3(demultiplexer_2_out3), .out4(demultiplexer_2_out4), .out5(demultiplexer_2_out5),
    .out6(demultiplexer_2_out6), .out7(demultiplexer_2_out7), .in(i_n), .sel(address[5:3]));
  Ram8 ram8_1 (
    .i_n(demultiplexer_2_out0), .address(address[2:0]), .load(demultiplexer_1_out0), .clock(clock),
    .out_5(ram8_1_out_5));
  Ram8 ram8_2 (
    .i_n(demultiplexer_2_out1), .address(address[2:0]), .load(demultiplexer_1_out1), .clock(clock),
    .out_5(ram8_2_out_5));
  Ram8 ram8_3 (
    .i_n(demultiplexer_2_out2), .address(address[2:0]), .load(demultiplexer_1_out2), .clock(clock),
    .out_5(ram8_3_out_5));
  Ram8 ram8_4 (
    .i_n(demultiplexer_2_out3), .address(address[2:0]), .load(demultiplexer_1_out3), .clock(clock),
    .out_5(ram8_4_out_5));
  Ram8 ram8_5 (
    .i_n(demultiplexer_2_out4), .address(address[2:0]), .load(demultiplexer_1_out4), .clock(clock),
    .out_5(ram8_5_out_5));
  Ram8 ram8_6 (
    .i_n(demultiplexer_2_out5), .address(address[2:0]), .load(demultiplexer_1_out5), .clock(clock),
    .out_5(ram8_6_out_5));
  Ram8 ram8_7 (
    .i_n(demultiplexer_2_out6), .address(address[2:0]), .load(demultiplexer_1_out6), .clock(clock),
    .out_5(ram8_7_out_5));
  Ram8 ram8_8 (
    .i_n(demultiplexer_2_out7), .address(address[2:0]), .load(demultiplexer_1_out7), .clock(clock),
    .out_5(ram8_8_out_5));
  Multiplexer #(.select(3), .width(16)) multiplexer_1 (
    .in0(ram8_1_out_5), .in1(ram8_2_out_5), .in2(ram8_3_out_5), .in3(ram8_4_out_5), .in4(ram8_5_out_5),
    .in5(ram8_6_out_5), .in6(ram8_7_out_5), .in7(ram8_8_out_5), .out(out_5), .sel(address[5:3]));
endmodule

module Ram512 (
  input  load,
  input  [15:0] i_n,
  input  [8:0] address,
  input  clock,
  output [15:0] out_5
);

  Demultiplexer #(.select(3)) demultiplexer_1 (
    .in(load), .sel(address[8:6]));  // open: out0, out1, out2, out3, out4, out5, out6, out7
  Demultiplexer #(.select(3), .width(16)) demultiplexer_2 (
    .in(i_n), .sel(address[8:6]));  // open: out0, out1, out2, out3, out4, out5, out6, out7
  Ram64 ram64_1 ();  // open: load, i_n, address, clock, out_5
  Ram64 ram64_2 ();  // open: load, i_n, address, clock, out_5
  Ram64 ram64_3 ();  // open: load, i_n, address, clock, out_5
  Ram64 ram64_4 ();  // open: load, i_n, address, clock, out_5
  Ram64 ram64_5 ();  // open: load, i_n, address, clock, out_5
  Ram64 ram64_6 ();  // open: load, i_n, address, clock, out_5
  Ram64 ram64_7 ();  // open: load, i_n, address, clock, out_5
  Ram64 ram64_8 ();  // open: load, i_n, address, clock, out_5
  Multiplexer #(.select(3), .width(16)) multiplexer_1 (
    .out(out_5), .sel(address[8:6]));  // open: in0, in1, in2, in3, in4, in5, in6, in7
endmodule

module PC (
  input  clock,
  input  [15:0] i_n,
  input  in_3,
  input  load,
  input  reset,
  output [15:0] out_6
);

  wire [15:0] and_1_out, inc_1_out_2, multiplexer_1_out, multiplexer_2_out, not_1_out, register16_1_ou_t;

  inc inc_1 (.in_1(i_n), .out_2(inc_1_out_2));
  assign and_1_out = i_n & not_1_out;  // AND_Gate and_1, 16 bits wide
  assign not_1_out = ~i_n;  // NOT_Gate not_1, 16 bits wide
  Multiplexer #(.width(16)) multiplexer_1 (.in0(i_n), .in1(inc_1_out_2), .out(multiplexer_1_out), .sel(in_3));
  Multiplexer #(.width(16)) multiplexer_2 (.in0(multiplexer_1_out), .in1(out_6), .out(multiplexer_2_out), .sel(load));
  register16 register16_1 (.load(load), .clock(clock), .in_3(multiplexer_2_out), .ou_t(register16_1_ou_t));
  Multiplexer #(.width(16)) multiplexer_3 (.in0(register16_1_ou_t), .in1(and_1_out), .out(out_6), .sel(reset));
endmodule

module inc (
  input  [15:0] in_1,
  output [15:0] out_2
);

  wire not_1_out;
  wire [15:0] or_1_out;

  not not_1 (not_1_out, in_1[0]);
  or or_1 (or_1_out[0], not_1_out, in_1[0]);
  not not_2 (or_1_out[15], or_1_out[0]);
  Adder #(.width(16)) adder_1 (.a({{15{or_1_out[15]}}, or_1_out[0]}), .b(in_1), .out(out_2));  // open: cin, cout
endmodule
