// Logisim project math.circ as structural Verilog
module halfadder (
  input  a,
  input  b,
  output carry,
  output sum
);

  and and_1 (carry, a, b);
  xor xor_1 (sum, a, b);
endmodule

module fulladder (
  input  a,
  input  b,
  input  c,
  output carry,
  output sum
);

  wire halfadder_1_carry, halfadder_1_sum, halfadder_2_carry;

  halfadder halfadder_1 (.a(a), .b(b), .carry(halfadder_1_carry), .sum(halfadder_1_sum));
  halfadder halfadder_2 (.a(halfadder_1_sum), .b(c), .carry(halfadder_2_carry), .sum(sum));
  or or_1 (carry, halfadder_1_carry, halfadder_2_carry);
endmodule

module add16 (
  input  [15:0] in_1,
  input  [15:0] in_2,
  output [15:0] out_3
);

  wire add16helper_1_carry, add16helper_2_carry, add16helper_3_carry, add16helper_4_carry,
       add16helper_5_carry, add16helper_6_carry, add16helper_7_carry, add16helper_8_carry,
       add16helper_9_carry, add16helper_10_carry, add16helper_11_carry, add16helper_12_carry,
       add16helper_13_carry, add16helper_15_carry, halfadder_1_carry;

  add16helper add16helper_1 (
    .b(in_2[1]), .a(in_1[1]), .incarry(halfadder_1_carry), .carry(add16helper_1_carry), .sum(out_3[1]));
  halfadder halfadder_1 (.a(in_1[0]), .b(in_2[0]), .carry(halfadder_1_carry), .sum(out_3[0]));
  add16helper add16helper_2 (
    .b(in_2[5]), .a(in_1[5]), .incarry(add16helper_3_carry), .carry(add16helper_2_carry), .sum(out_3[5]));
  add16helper add16helper_3 (
    .b(in_2[4]), .a(in_1[4]), .incarry(add16helper_4_carry), .carry(add16helper_3_carry), .sum(out_3[4]));
  add16helper add16helper_4 (
    .b(in_2[3]), .a(in_1[3]), .incarry(add16helper_5_carry), .carry(add16helper_4_carry), .sum(out_3[3]));
  add16helper add16helper_5 (
    .b(in_2[2]), .a(in_1[2]), .incarry(add16helper_1_carry), .carry(add16helper_5_carry), .sum(out_3[2]));
  add16helper add16helper_6 (
    .b(in_2[9]), .a(in_1[9]), .incarry(add16helper_7_carry), .carry(add16helper_6_carry), .sum(out_3[9]));
  add16helper add16helper_7 (
    .b(in_2[8]), .a(in_1[8]), .incarry(add16helper_8_carry), .carry(add16helper_7_carry), .sum(out_3[8]));
  add16helper add16helper_8 (
    .b(in_2[7]), .a(in_1[7]), .incarry(add16helper_9_carry), .carry(add16helper_8_carry), .sum(out_3[7]));
  add16helper add16helper_9 (
    .b(in_2[6]), .a(in_1[6]), .incarry(add16helper_2_carry), .carry(add16helper_9_carry), .sum(out_3[6]));
  add16helper add16helper_10 (
    .b(in_2[13]), .a(in_1[13]), .incarry(add16helper_11_carry), .carry(add16helper_10_carry), .sum(out_3[13]));
  add16helper add16helper_11 (
    .b(in_2[12]), .a(in_1[12]), .incarry(add16helper_12_carry), .carry(add16helper_11_carry), .sum(out_3[12]));
  add16helper add16helper_12 (
    .b(in_2[11]), .a(in_1[11]), .incarry(add16helper_13_carry), .carry(add16helper_12_carry), .sum(out_3[11]));
  add16helper add16helper_13 (
    .b(in_2[10]), .a(in_1[10]), .incarry(add16helper_6_carry), .carry(add16helper_13_carry), .sum(out_3[10]));
  add16helper add16helper_14 (
    .b(in_2[15]), .a(in_1[15]), .incarry(add16helper_15_carry), .sum(out_3[15]));  // open: carry
  add16helper add16helper_15 (
    .b(in_2[14]), .a(in_1[14]), .incarry(add16helper_10_carry), .carry(add16helper_15_carry), .sum(out_3[14]));
endmodule

module add16helper (
  input  a,
  input  b,
  input  incarry,
  output carry,
  output sum
);

  wire halfadder_1_carry, halfadder_1_sum, halfadder_2_carry;

  halfadder halfadder_1 (.a(a), .b(b), .carry(halfadder_1_carry), .sum(halfadder_1_sum));
  or or_1 (carry, halfadder_1_carry, halfadder_2_carry);
  halfadder halfadder_2 (.a(halfadder_1_sum), .b(incarry), .carry(halfadder_2_carry), .sum(sum));
endmodule

module inc16 (
  input  [15:0] in_1,
  output [15:0] out_2
);

  wire not_1_out;
  wire [15:0] or_1_out;

  not not_1 (not_1_out, in_1[0]);
  or or_1 (or_1_out[0], not_1_out, in_1[0]);
  not not_2 (or_1_out[15], or_1_out[0]);
  add16 add16_1 (.in_1({{15{or_1_out[15]}}, or_1_out[0]}), .in_2(in_1), .out_3(out_2));
endmodule

module alu (
  input  ny,
  input  z_x,
  input  n_x,
  input  zy,
  input  eff,
  input  no,
  input  [15:0] x,
  input  [15:0] y,
  output [15:0] ou_t,
  output zr,
  output out_11
);

  wire [15:0] f_1_out_4, not_1_out, nx_1_out_3, nx_2_out_3, zx_1_out_3, zx_2_out_3;

  zx zx_1 (.z_x(z_x), .x(x), .out_3(zx_1_out_3));
  nx nx_1 (.n_x(n_x), .x(zx_1_out_3), .out_3(nx_1_out_3));
  zx zx_2 (.z_x(zy), .x(y), .out_3(zx_2_out_3));
  nx nx_2 (.n_x(ny), .x(zx_2_out_3), .out_3(nx_2_out_3));
  f f_1 (.x(nx_1_out_3), .y(nx_2_out_3), .f_f(eff), .out_4(f_1_out_4));
  nx nx_3 (.n_x(no), .x(f_1_out_4), .out_3(ou_t));
  assign not_1_out = ~ou_t;  // NOT_Gate not_1, 16 bits wide
  and and_1 (zr, not_1_out[15], not_1_out[14], not_1_out[13], not_1_out[12], not_1_out[11], not_1_out[10], not_1_out[9], not_1_out[8], not_1_out[6], not_1_out[5], not_1_out[4], not_1_out[3], not_1_out[2], not_1_out[1], not_1_out[0], not_1_out[7]);

  assign out_11 = ou_t[15];
endmodule

module zx (
  input  [15:0] x,
  input  z_x,
  output [15:0] out_3
);

  wire not_1_out;
  wire [15:0] to16_1_out_2;

  not not_1 (not_1_out, z_x);
  to16 to16_1 (.in_1(not_1_out), .out_2(to16_1_out_2));
  Multiplexer #(.width(16)) multiplexer_1 (.in0(x), .in1(to16_1_out_2), .out(out_3), .sel(z_x));
endmodule

module to16 (
  input  in_1,
  output [15:0] out_2
);


  assign out_2 = {16{in_1}};
endmodule

module nx (
  input  n_x,
  input  [15:0] x,
  output [15:0] out_3
);

  wire [15:0] not_1_out;

  assign not_1_out = ~x;  // NOT_Gate not_1, 16 bits wide
  Multiplexer #(.width(16)) multiplexer_1 (.in0(x), .in1(not_1_out), .out(out_3), .sel(n_x));
endmodule

module f (
  input  [15:0] x,
  input  [15:0] y,
  input  f_f,
  output [15:0] out_4
);

  wire [15:0] add_out_3, and_1_out;

  assign and_1_out = y & x;  // AND_Gate and_1, 16 bits wide
  add16 add (.in_1(y), .in_2(x), .out_3(add_out_3));
  Multiplexer #(.width(16)) multiplexer_1 (.in0(and_1_out), .in1(add_out_3), .out(out_4), .sel(f_f));
endmodule
